# Fritzing sketch Fritzing-Satelite-Tracking (saved by Fritzing 0.9.2b)

parts:
  Componente1 = Arduino Uno (Rev3)
  Motor_28ybj-48 = Stepper Motor - Bipolar
  RE1 = Rotary Encoder [package=THT]
  R1 = Resistor [tolerance=±5% resistance=220 package=THT]
  J1 = female pin header, 2 pins [form="♀ (female)"]  # not connected
  J2 = female pin header, 2 pins [form="♀ (female)"]
  J3 = female pin header, 2 pins [form="♀ (female)"]
  J4 = female pin header, 2 pins [form="♀ (female)"]
  J5 = female pin header, 2 pins [form="♀ (female)"]
  J6 = female pin header, 2 pins [form="♀ (female)"]
  J7 = female pin header, 2 pins [form="♀ (female)"]  # not connected
  J8 = female pin header, 2 pins [form="♀ (female)"]
  Power_plug1 = Power plug  # not connected

nets:
  N1: Componente1.A0, RE1.EncoderPinC
  N2: Componente1.D8, Motor_28ybj-48.D
  N3: Componente1.D9_PWM, Motor_28ybj-48.B
  N4: Componente1.D10_PWM/SS, Motor_28ybj-48.C
  N5: Componente1.D11_PWM/MOSI, Motor_28ybj-48.A
  N6: Componente1.D2, J6.pin1
  N7: Componente1.D3_PWM, J5.pin1
  N8: Componente1.D4, J4.pin1
  N9: Componente1.D5_PWM, J3.pin1
  N10: Componente1.D6_PWM, J2.pin1
  N11: Componente1.5V, RE1.EncoderPinB
  N12: Componente1.GND, RE1.EncoderPinA
  N13: R1.Pin_0, J8.pin2

notes:
  IN4
  IN3
  IN2
  IN1
  CE
  RST
  DC
  DIN
  CLK
  GND
  BL
  VCC 5V
  LIGACOES PARA O LCD NOKIA 5110
  LCD
  + 5V
  MOTOR DE PASSO
  28BJY-48 (5V)
  POTENCIOMENTO 10K
  POTENCIOMENTO USADO PARA CONTROLE MANUAL DO MOTOR DE PASSO
  CONTROLANDO O AZIMUTE MANUAL
